# Fritzing sketch klumhas (saved by Fritzing 0.9.3b)
stripboards: 1

parts:
  U1 = atmega328 [package=dip]
  XTAL1 = Crystal [frequency="16 Mhz" package=THT]
  C2 = Capacitor [package=cap-pth-small2]
  R1 = Resistor [tolerance=±5% resistance=10k package="0402 [SMD]"]
  JP3 = Header 12 [package=1x12_machine-pin-header_lock.004]
  C1 = Capacitor [package=cap-pth-small2]
  R2 = Resistor [tolerance=±5% resistance=220 package=THT]
  LED1 = smd LED [color="Red (633nm)" package="1206 [SMD]"]
  VCC1 = Battery
  DS1 = DS18B20 1-Wire Temperature Sensor [part_number=DS18B20]
  R3 = Resistor [tolerance=±5% resistance=220 package="0402 [SMD]"]
  Part1 = NRF24L01
  Grove1 = Grove OLED 128x96

nets:
  N1: U1.RESET, R1.Pin_0, JP3.1
  N2: U1.D0_(RX), JP3.2
  N3: U1.D1_(TX), JP3.3
  N4: U1.D2, JP3.4
  N5: U1.D3_(PWM), U1.D4, JP3.5, JP3.6
  3.3V: U1.VCC, U1.AVCC, R1.Pin_1, JP3.7, VCC1.+, DS1.VDD, R3.Pin_1, Part1.VCC, Grove1.VCC
  GND: U1.GND, C2.1, JP3.8, C1.1, R2.Pin_1, VCC1.-, DS1.GND, Part1.GND, Grove1.GND
  N6: U1.XLAT1, XTAL1.pin_0, C2.2, JP3.9
  N7: U1.XLAT2, XTAL1.pin_1, JP3.10, C1.2
  N8: U1.D5_(PWM), JP3.11, DS1.DQ, R3.Pin_0
  N9: U1.D6_(PWM), JP3.12
  N10: U1.D7, Part1.CE
  N11: U1.D8, Part1.CSN
  N12: U1.D9_(PWM), LED1.cathode
  N13: U1.D11_(PWM), Part1.MOSI
  N14: U1.D12, Part1.MISO
  N15: U1.D13, Part1.SCK
  N16: U1.A4, Grove1.SDA
  N17: U1.A5, Grove1.SCL
  N18: R2.Pin_0, LED1.anode
